# Fritzing sketch ArduinoMKRWifi1010_NeopixelStrip (saved by Fritzing 0.9.3b)
breadboards: 1

parts:
  Mod1 = Arduino MKR Wifi 1010
  Neopixel_strip_(WS2812B)_>=_60_pixels = Neopixel Strip -- Black (30/m)

nets:
  GND: Mod1.GND, Neopixel_strip_(WS2812B)_>=_60_pixels.GND
  N1: Mod1.~D5, Neopixel_strip_(WS2812B)_>=_60_pixels.Din
  +5V: Mod1.+5V, Neopixel_strip_(WS2812B)_>=_60_pixels.+5V

custom parts:
  Arduino MKR Wifi 1010: Arduino MKR Wifi 1010, SAMD21 Cortex-M0+ 32bit Low Power ARM MCU,Flash Memory 256 KB, SRAM 32KB, 48mhz clock, Ublok Wifi interface.
  Neopixel Strip -- Black (30/m): These NeoPixel strips have 30 digitally-addressable pixel LEDs per meter and are very affordable and are only 12.5 mm wide, 10 mm if you remove the strip from the casing.
