# Fritzing sketch ArduinoKMR1010-moisture-and-BME280 (saved by Fritzing 0.9.3b)
breadboards: 1

parts:
  Part1 = BME280 Breakout
  Mod1 = Arduino MKR Wifi 1010
  Capacitive_Soil_Moisture_Sensor1 = DFRobot Capacitive Soil Moisture Sensor V1.0 [part_number=SEN0193]
  Part2 = Lithium Ion Polymer Battery 3.7v 500mAh [part_number=1578]

nets:
  GND: Part1.GND, Mod1.GND, Capacitive_Soil_Moisture_Sensor1.GND, Part2.negative
  3.3V: Part1.3.3V, Mod1.+3V3
  N1: Part1.SDI/SDA, Mod1.D11/SDA
  N2: Part1.SCK/SCL, Mod1.D12/SCL
  N3: Mod1.LI-PO+, Part2.positive
  N4: Mod1.A0/DAC0, Capacitive_Soil_Moisture_Sensor1.A
  +5V: Mod1.+5V, Capacitive_Soil_Moisture_Sensor1.VCC

custom parts:
  Arduino MKR Wifi 1010: Arduino MKR Wifi 1010, SAMD21 Cortex-M0+ 32bit Low Power ARM MCU,Flash Memory 256 KB, SRAM 32KB, 48mhz clock, Ublok Wifi interface.
  DFRobot Capacitive Soil Moisture Sensor V1.0: DFRobot Capacitive Soil Moisture Sensor V1.0 This product measures soil moisture levels by capacitive sensing, rather than resistive sensing like other types of moisture sensor. It is made of a corrosion resistant material giving it a long service life. Insert it into soil and impress your friends with the real-time soil moisture data! The product includes an on-board voltage regulator which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
  Lithium Ion Polymer Battery 3.7v 500mAh: Lithium ion polymer (also known as 'lipo' or 'lipoly') batteries are thin, light and powerful. The output ranges from 4.2V when completely charged to 3.7V. This battery has a capacity of 500mAh for a total of about 1.9 Wh. The batteries come pre-attached with a genuine 2-pin JST-PH connector as shown and include the necessary protection circuitry.
