# Fritzing sketch esp32-IR-receiver (saved by Fritzing 0.9.3b)
breadboards: 1

parts:
  IR1_-_check_attached_svg_for_pinout = TSOP312.., 314.. [package=THT]
  U1 = ESP32-38PinWide [part_number=ESP32-38PinWide]

nets:
  N1: IR1_-_check_attached_svg_for_pinout.GND, U1.GPIO14
  N2: IR1_-_check_attached_svg_for_pinout.Vs, U1.GND
  N3: IR1_-_check_attached_svg_for_pinout.Data, U1.3.3

custom parts:
  ESP32-38PinWide: Generic 38-Pin ESP32 with wide format (only access to one side of pins on a breadboard) based on Stephen Lilley's HiLetgo ESP-WROOM-32 ESP32 ESP-32S Development Board.
