# Fritzing sketch ArduinoNano33Iot_bme280_temp_hum_press_sensor (saved by Fritzing 0.9.3b)
breadboards: 1

parts:
  Part1 = Arduino Nano 33 IOT
  Part2 = BME280 Breakout

nets:
  N1: Part1.RESET, Part1.A7
  GND: Part1.GND, Part1.D13~, Part2.GND
  N2: Part1.D11/MOSI, Part1.+5V
  N3: Part1.A5, Part2.SCK/SCL
  N4: Part1.A4, Part2.SDI/SDA
  3V3: Part1.3V3, Part2.3.3V

custom parts:
  Arduino Nano 33 IOT: The Arduino Nano 33 IoT is the easiest and cheapest point of entry to enhance existing devices (and creating new ones) to be part of the IoT and designing pico-network applications. Whether you are looking at building a sensor network connected to your office or home router, or if you want to create a BLE device sending data to a cellphone, the Nano 33 IoT is your one-stop-solution for many of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
